// Logisim project 2logism file-completed 4nibble RAM.circ as structural Verilog: 3 circuits, main circuit main
module main (
  input  [1:0] Address,
  input  [3:0] Data,
  input  in_3,
  output [3:0] Output
);

  wire and_1_out, and_2_out, and_3_out, and_4_out, and_5_out, and_6_out, and_7_out, and_8_out, and_9_out,
       and_10_out, and_11_out, and_12_out, and_13_out, and_14_out, and_15_out, and_16_out, and_17_out,
       and_18_out, and_19_out, and_20_out, and_21_out, and_22_out, and_23_out, and_24_out, and_25_out,
       and_26_out, and_27_out, and_28_out, clock_1_out, d_ff_1_q, d_ff_2_q, d_ff_3_q, d_ff_4_q, d_ff_5_q,
       d_ff_6_q, d_ff_7_q, d_ff_8_q, d_ff_9_q, d_ff_10_q, d_ff_11_q, d_ff_12_q, d_ff_13_q, d_ff_14_q,
       d_ff_15_q, d_ff_16_q, data_register_1_out_11, data_register_1_out_12, data_register_1_out_13,
       data_register_1_out_14, not_1_out, not_2_out, not_3_out, not_4_out, not_5_out, not_6_out, or_1_out,
       or_2_out, or_3_out, or_4_out;

  not not_1 (not_1_out, Address[1]);
  not not_2 (not_2_out, Address[0]);
  Clock clock_1 (.out(clock_1_out));
  Data_Register data_register_1 (
    .R_W(in_3), .clock(clock_1_out), .in_5(or_4_out), .in_6(or_3_out), .in_7(or_2_out), .in_8(or_1_out),
    .out_11(data_register_1_out_11), .out_12(data_register_1_out_12), .out_13(data_register_1_out_13),
    .out_14(data_register_1_out_14), .in_1(Data[3]), .in_2(Data[2]), .in_3(Data[1]), .in_4(Data[0]));
  and and_1 (and_1_out, clock_1_out, not_1_out, not_2_out);
  and and_2 (and_2_out, clock_1_out, not_1_out, Address[0]);
  and and_3 (and_3_out, clock_1_out, Address[1], not_2_out);
  and and_4 (and_4_out, clock_1_out, Address[1], Address[0]);
  and and_5 (and_5_out, in_3, and_1_out);
  and and_6 (and_6_out, in_3, and_2_out);
  and and_7 (and_7_out, in_3, and_3_out);
  and and_8 (and_8_out, in_3, and_4_out);
  Read_Ouput_Regulator read_ouput_regulator_1 (
    .in_1(data_register_1_out_14), .in_2(data_register_1_out_13), .in_3(data_register_1_out_12),
    .in_4(data_register_1_out_11), .in_5(in_3), .out_6(Output[3]), .out_7(Output[2]), .out_8(Output[1]),
    .out_9(Output[0]));
  D_Flip_Flop d_ff_1 (.clk(and_5_out), .D(data_register_1_out_11), .Q(d_ff_1_q));  // open: Qn, preset, en, reset
  D_Flip_Flop d_ff_2 (.clk(and_5_out), .D(data_register_1_out_12), .Q(d_ff_2_q));  // open: Qn, preset, en, reset
  D_Flip_Flop d_ff_3 (.clk(and_5_out), .D(data_register_1_out_13), .Q(d_ff_3_q));  // open: Qn, preset, en, reset
  D_Flip_Flop d_ff_4 (.clk(and_5_out), .D(data_register_1_out_14), .Q(d_ff_4_q));  // open: Qn, preset, en, reset
  D_Flip_Flop d_ff_5 (.clk(and_6_out), .D(data_register_1_out_11), .Q(d_ff_5_q));  // open: Qn, preset, en, reset
  D_Flip_Flop d_ff_6 (.clk(and_6_out), .D(data_register_1_out_12), .Q(d_ff_6_q));  // open: Qn, preset, en, reset
  D_Flip_Flop d_ff_7 (.clk(and_6_out), .D(data_register_1_out_13), .Q(d_ff_7_q));  // open: Qn, preset, en, reset
  D_Flip_Flop d_ff_8 (.clk(and_6_out), .D(data_register_1_out_14), .Q(d_ff_8_q));  // open: Qn, preset, en, reset
  D_Flip_Flop d_ff_9 (.clk(and_7_out), .D(data_register_1_out_11), .Q(d_ff_9_q));  // open: Qn, preset, en, reset
  D_Flip_Flop d_ff_10 (.clk(and_7_out), .D(data_register_1_out_12), .Q(d_ff_10_q));  // open: Qn, preset, en, reset
  D_Flip_Flop d_ff_11 (.clk(and_7_out), .D(data_register_1_out_13), .Q(d_ff_11_q));  // open: Qn, preset, en, reset
  D_Flip_Flop d_ff_12 (.clk(and_7_out), .D(data_register_1_out_14), .Q(d_ff_12_q));  // open: Qn, preset, en, reset
  D_Flip_Flop d_ff_13 (.clk(and_8_out), .D(data_register_1_out_11), .Q(d_ff_13_q));  // open: Qn, preset, en, reset
  D_Flip_Flop d_ff_14 (.clk(and_8_out), .D(data_register_1_out_12), .Q(d_ff_14_q));  // open: Qn, preset, en, reset
  D_Flip_Flop d_ff_15 (.clk(and_8_out), .D(data_register_1_out_13), .Q(d_ff_15_q));  // open: Qn, preset, en, reset
  D_Flip_Flop d_ff_16 (.clk(and_8_out), .D(data_register_1_out_14), .Q(d_ff_16_q));  // open: Qn, preset, en, reset
  not not_3 (not_3_out, in_3);
  not not_4 (not_4_out, in_3);
  not not_5 (not_5_out, in_3);
  not not_6 (not_6_out, in_3);
  or or_1 (or_1_out, and_16_out, and_15_out, and_14_out, and_13_out);
  and and_9 (and_9_out, not_3_out, and_1_out);
  and and_10 (and_10_out, not_4_out, and_2_out);
  and and_11 (and_11_out, not_5_out, and_3_out);
  and and_12 (and_12_out, not_6_out, and_4_out);
  or or_2 (or_2_out, and_20_out, and_19_out, and_18_out, and_17_out);
  and and_13 (and_13_out, d_ff_1_q, and_9_out);
  and and_14 (and_14_out, d_ff_5_q, and_10_out);
  and and_15 (and_15_out, d_ff_9_q, and_11_out);
  and and_16 (and_16_out, d_ff_13_q, and_12_out);
  or or_3 (or_3_out, and_24_out, and_23_out, and_22_out, and_21_out);
  and and_17 (and_17_out, d_ff_2_q, and_9_out);
  and and_18 (and_18_out, d_ff_6_q, and_10_out);
  and and_19 (and_19_out, d_ff_10_q, and_11_out);
  and and_20 (and_20_out, d_ff_14_q, and_12_out);
  and and_21 (and_21_out, d_ff_3_q, and_9_out);
  and and_22 (and_22_out, d_ff_7_q, and_10_out);
  and and_23 (and_23_out, d_ff_11_q, and_11_out);
  and and_24 (and_24_out, d_ff_15_q, and_12_out);
  or or_4 (or_4_out, and_28_out, and_27_out, and_26_out, and_25_out);
  and and_25 (and_25_out, d_ff_4_q, and_9_out);
  and and_26 (and_26_out, d_ff_8_q, and_10_out);
  and and_27 (and_27_out, d_ff_12_q, and_11_out);
  and and_28 (and_28_out, d_ff_16_q, and_12_out);

  // Notes on the sheet:
  //   Mode (1=write,0=read)
  //   Clock
  //   Please allow a couple of clock cycles for the read-output to stabalize, thanks
endmodule

module Data_Register (
  input  in_1,
  input  in_2,
  input  in_3,
  input  in_4,
  input  in_5,
  input  in_6,
  input  in_7,
  input  in_8,
  input  R_W,
  input  clock,
  output out_11,
  output out_12,
  output out_13,
  output out_14
);

  wire and_1_out, and_2_out, and_3_out, and_4_out, and_5_out, and_6_out, and_7_out, and_8_out, not_1_out,
       not_2_out, not_3_out, not_4_out, or_1_out, or_2_out, or_3_out, or_4_out;

  not not_1 (not_1_out, R_W);
  and and_1 (and_1_out, in_1, R_W);
  or or_1 (or_1_out, and_1_out, and_2_out);
  and and_2 (and_2_out, not_1_out, in_5);
  D_Flip_Flop #(.trigger("falling")) d_ff_1 (.clk(clock), .D(or_1_out), .Q(out_11));  // open: Qn, preset, en, reset
  not not_2 (not_2_out, R_W);
  and and_3 (and_3_out, not_2_out, in_6);
  and and_4 (and_4_out, in_2, R_W);
  or or_2 (or_2_out, and_4_out, and_3_out);
  D_Flip_Flop #(.trigger("falling")) d_ff_2 (.clk(clock), .D(or_2_out), .Q(out_12));  // open: Qn, preset, en, reset
  and and_5 (and_5_out, in_3, R_W);
  not not_3 (not_3_out, R_W);
  and and_6 (and_6_out, not_3_out, in_7);
  or or_3 (or_3_out, and_5_out, and_6_out);
  D_Flip_Flop #(.trigger("falling")) d_ff_3 (.clk(clock), .D(or_3_out), .Q(out_13));  // open: Qn, preset, en, reset
  not not_4 (not_4_out, R_W);
  and and_7 (and_7_out, in_4, R_W);
  or or_4 (or_4_out, and_7_out, and_8_out);
  and and_8 (and_8_out, not_4_out, in_8);
  D_Flip_Flop #(.trigger("falling")) d_ff_4 (.clk(clock), .D(or_4_out), .Q(out_14));  // open: Qn, preset, en, reset

  // Notes on the sheet:
  //   inputs:data to be written
  //   inputs: data being read
endmodule

module Read_Ouput_Regulator (
  input  in_1,
  input  in_2,
  input  in_3,
  input  in_4,
  input  in_5,
  output out_6,
  output out_7,
  output out_8,
  output out_9
);

  wire not_1_out;

  not not_1 (not_1_out, in_5);
  and and_1 (out_6, not_1_out, in_1);
  and and_2 (out_7, not_1_out, in_2);
  and and_3 (out_8, not_1_out, in_3);
  and and_4 (out_9, not_1_out, in_4);
endmodule
